# Fritzing sketch raspberry_pi_ds18b20_3 (saved by Fritzing 0.9.2b)
breadboards: 1

parts:
  DS1 = DS18B20 1-Wire Temperature Sensor [part_number=DS18B20]
  RaspberryPi1 = Raspberry Pi Model B
  R1 = Resistor [tolerance=±5% resistance=4.7k package=THT]

nets:
  VDD: DS1.VDD, RaspberryPi1.3V3, R1.Pin_0
  N1: DS1.DQ, RaspberryPi1.#4, R1.Pin_1
  GND: DS1.GND, RaspberryPi1.GND

custom parts:
  Raspberry Pi Model B: Raspberry Pi (Model B)
