# Fritzing sketch raspberry_pi_ds18b20_4 (saved by Fritzing 0.9.2b)
breadboards: 1

parts:
  Raspberry_Pi2 = Raspberry Pi B rev2
  DS3 = DS18B20 1-Wire Temperature Sensor [part_number=DS18B20]
  R2 = Resistor [tolerance=±5% resistance=4.7k package=THT]

nets:
  3V3: Raspberry_Pi2.3V3, DS3.VDD, R2.Pin_1
  N1: Raspberry_Pi2.GPIO_4, DS3.DQ, R2.Pin_0
  GND: Raspberry_Pi2.GND, DS3.GND
